# Fritzing sketch proto_parking (saved by Fritzing 1.0.6)
perfboards: 1

parts:
  HC-SR04_Sensor_1 = HC-SR04 Ultrasonic Distance Sensor  # not connected
  ArduinoNano1 = Arduino Nano (Rev3.0)
  RS485_module1 = RS485 Module (MAX3485)  # not connected
  Switch-button = Pushbutton [package="[THT]"]
  J-radar = female pin header, 4 pins [form="♀ (female)"]
  J-display = female pin header, 4 pins [form="♀ (female)"]
  J-leds = female pin header, 4 pins [form="♀ (female)"]
  J-ttl-rs485 = female pin header, 4 pins [form="♀ (female)"]
  J1 = Camdenboss CTB0158-4 [part_number=CTB0158-4 package=THT]
  J-ab-rs485 = female pin header, 4 pins [form="♀ (female)"]
  J3 = Camdenboss CTB0158-4 [part_number=CTB0158-4 package=THT]
  J-ard-nano-a = female pin header, 15 pins [form="♀ (female)"]
  J-ard-nano-b = female pin header, 15 pins [form="♀ (female)"]
  power_converter = RioRand LM2596  # not connected
  J-swbt-b-1 = female pin header, 1 pin [form="♀ (female)"]
  J-swbt-b-2 = female pin header, 1 pin [form="♀ (female)"]
  J-swbt-a-1 = female pin header, 1 pin [form="♀ (female)"]
  J-swbt-a-2 = female pin header, 1 pin [form="♀ (female)"]
  J-src-vcc = female pin header, 1 pin [form="♀ (female)"]
  J-src-gnd = female pin header, 1 pin [form="♀ (female)"]
  J-vcc = female pin header, 1 pin [form="♀ (female)"]
  J-gnd = female pin header, 1 pin [form="♀ (female)"]
  OLED_I2C1 = OLED 128x64 I2C Monochrome Display  # not connected

nets:
  N1: ArduinoNano1.D1/TX, J-ard-nano-a.pin1
  N2: ArduinoNano1.D0/RX, J-ard-nano-a.pin2
  N3: ArduinoNano1.RESET, J-ard-nano-a.pin3, J-ard-nano-b.pin13
  gnd/src-gnd: ArduinoNano1.GND, Switch-button.Pin_1, Switch-button.Pin_2, J-radar.pin4, J-display.pin1, J-leds.pin1, J1.pin4, J-ab-rs485.pin4, J3.pin4, J-ard-nano-a.pin4, J-ard-nano-b.pin14, J-swbt-a-1.pin1, J-swbt-a-2.pin1, J-src-gnd.pin1, J-gnd.pin1
  trigger-radar: ArduinoNano1.D2, J-radar.pin2, J-ard-nano-a.pin5
  echo-radar: ArduinoNano1.D3, J-radar.pin3, J-ard-nano-a.pin6
  red-led: ArduinoNano1.D4, J-leds.pin2, J-ard-nano-a.pin7
  yellow-led: ArduinoNano1.D5, J-leds.pin3, J-ard-nano-a.pin8
  green-led: ArduinoNano1.D6, J-leds.pin4, J-ard-nano-a.pin9
  switch-pin-a: ArduinoNano1.D7, Switch-button.Pin_3, Switch-button.Pin_4, J-ard-nano-a.pin10, J-swbt-b-1.pin1, J-swbt-b-2.pin1
  N4: ArduinoNano1.D8, J-ard-nano-a.pin11
  dere-rs485: ArduinoNano1.D9, J-ttl-rs485.pin2, J-ttl-rs485.pin3, J-ard-nano-a.pin12
  ro-rs485: ArduinoNano1.D10, J-ttl-rs485.pin4, J-ard-nano-a.pin13
  di-rs485: ArduinoNano1.D11/MOSI, J-ttl-rs485.pin1, J-ard-nano-a.pin14
  N5: ArduinoNano1.D12/MISO, J-ard-nano-a.pin15
  vcc: ArduinoNano1.VIN, J-radar.pin1, J-display.pin2, J-ab-rs485.pin1, J-ard-nano-b.pin15, J-vcc.pin1
  N6: ArduinoNano1.5V, J-ard-nano-b.pin12
  N7: ArduinoNano1.A7, J-ard-nano-b.pin11
  N8: ArduinoNano1.A6, J-ard-nano-b.pin10
  scl-display: ArduinoNano1.A5, J-display.pin3, J-ard-nano-b.pin9
  sda-display: ArduinoNano1.A4, J-display.pin4, J-ard-nano-b.pin8
  N9: ArduinoNano1.A3, J-ard-nano-b.pin7
  N10: ArduinoNano1.A2, J-ard-nano-b.pin6
  N11: ArduinoNano1.A1, J-ard-nano-b.pin5
  N12: ArduinoNano1.A0, J-ard-nano-b.pin4
  N13: ArduinoNano1.AREF, J-ard-nano-b.pin3
  N14: ArduinoNano1.3V3, J-ard-nano-b.pin2
  N15: ArduinoNano1.D13/SCK, J-ard-nano-b.pin1
  src-vcc: J1.pin1, J3.pin1, J-src-vcc.pin1
  b-rs485: J1.pin2, J-ab-rs485.pin2, J3.pin2
  a-rs485: J1.pin3, J-ab-rs485.pin3, J3.pin3

notes:
  HC-SR04
  VCC / GND
  5V / GND
  Trig
  D2
  Trigger Pulse
  Echo
  D3
  Echo Pulse
  OLED (I2C)
  VCC / GND
  5V / GND
  SCL
  A5
  Hardware I2C Clock
  SDA
  A4
  Hardware I2C Data
  RS485 TTL
  VCC / GND
  5V / GND
  DI (Data In)
  D11
  TX (Using SoftwareSerial)
  RO (Rec Out)
  D10
  RX (Using SoftwareSerial)
  DE / RE
  D9
  Flow Control (Jumpered together)
  RGB Traffic Light
  red/yel/gr n
  D4, D5, D6
  Digital Outputs
  GND
  GND
  Common Cathode
  Switch Button
  Pin A
  D7
  Use INPUT_PULLUP in code
  Pin B
  GND
  Connects to Ground when pressed

custom parts:
  RS485 Module (MAX3485): Commercially available RS485 to RS232 TTL Module
